// Logisim project Logic Unit.circ as structural Verilog
module Logic_Unit (
  input  [3:0] A0_A3,
  input  [3:0] B0_B3,
  input  S0,
  input  S1,
  output [3:0] out_5
);

  wire [3:0] and_1_out, not_1_out, or_1_out, xor_1_out;

  assign and_1_out = A0_A3 & B0_B3;  // AND_Gate and_1, 4 bits wide
  assign or_1_out = A0_A3 | B0_B3;  // OR_Gate or_1, 4 bits wide
  assign xor_1_out = A0_A3 ^ B0_B3;  // XOR_Gate xor_1, 4 bits wide
  assign not_1_out = ~A0_A3;  // NOT_Gate not_1, 4 bits wide
  _4x4_MUX u_4x4_mux_1 (
    .in_1(and_1_out[0]), .in_2(and_1_out[1]), .in_3(and_1_out[2]), .in_4(and_1_out[3]), .in_5(or_1_out[0]),
    .in_6(or_1_out[1]), .in_7(or_1_out[2]), .in_8(or_1_out[3]), .in_9(xor_1_out[0]), .in_10(xor_1_out[1]),
    .in_11(xor_1_out[2]), .in_12(xor_1_out[3]), .in_13(not_1_out[0]), .in_14(not_1_out[1]),
    .in_15(not_1_out[2]), .in_16(not_1_out[3]), .in_17(S0), .in_18(S1), .Y0(out_5[0]), .Y1(out_5[1]),
    .Y2(out_5[2]), .Y3(out_5[3]));

  // Notes on the sheet:
  //   AND
  //   OR
  //   XOR
  //   1's Comp
endmodule

module _4x4_MUX (
  input  in_1,
  input  in_2,
  input  in_3,
  input  in_4,
  input  in_5,
  input  in_6,
  input  in_7,
  input  in_8,
  input  in_9,
  input  in_10,
  input  in_11,
  input  in_12,
  input  in_13,
  input  in_14,
  input  in_15,
  input  in_16,
  input  in_17,
  input  in_18,
  output Y0,
  output Y1,
  output Y2,
  output Y3
);

  wire and_1_out, and_2_out, and_3_out, and_4_out, and_5_out, and_6_out, and_7_out, and_8_out, and_9_out,
       and_10_out, and_11_out, and_12_out, and_13_out, and_14_out, and_15_out, and_16_out, not_1_out,
       not_2_out, not_3_out;

  not not_1 (not_1_out, in_17);
  not not_2 (not_2_out, not_1_out);
  not not_3 (not_3_out, in_18);
  and and_1 (and_1_out, in_1, not_1_out, not_3_out);
  and and_2 (and_2_out, in_2, not_1_out, not_3_out);
  and and_3 (and_3_out, in_3, not_1_out, not_3_out);
  and and_4 (and_4_out, in_4, not_1_out, not_3_out);
  and and_5 (and_5_out, in_5, not_1_out, in_18);
  and and_6 (and_6_out, in_6, not_1_out, in_18);
  and and_7 (and_7_out, in_7, not_1_out, in_18);
  and and_8 (and_8_out, in_8, not_1_out, in_18);
  and and_9 (and_9_out, in_9, not_2_out, not_3_out);
  and and_10 (and_10_out, in_10, not_2_out, not_3_out);
  and and_11 (and_11_out, in_11, not_2_out, not_3_out);
  and and_12 (and_12_out, in_12, not_2_out, not_3_out);
  and and_13 (and_13_out, in_13, not_2_out, in_18);
  and and_14 (and_14_out, in_14, not_2_out, in_18);
  and and_15 (and_15_out, in_15, not_2_out, in_18);
  and and_16 (and_16_out, in_16, not_2_out, in_18);
  or or_1 (Y0, and_1_out, and_5_out, and_9_out, and_13_out);
  or or_2 (Y1, and_2_out, and_6_out, and_10_out, and_14_out);
  or or_3 (Y2, and_3_out, and_7_out, and_11_out, and_15_out);
  or or_4 (Y3, and_4_out, and_8_out, and_12_out, and_16_out);
endmodule
