// Logisim project Problem 2.circ as structural Verilog: 1 circuit, main circuit main
module main (
  input  X,
  input  E,
  output Q,
  output Q_prime,
  output Q_2,
  output Q_prime_2
);

  wire and_1_out, and_2_out, and_3_out, clock_1_out, not_1_out, not_2_out, or_1_out;

  not not_1 (not_1_out, X);
  and and_1 (and_1_out, not_1_out, not_2_out);
  and and_2 (and_2_out, X, Q_2);
  or or_1 (or_1_out, and_1_out, and_2_out);
  and and_3 (and_3_out, or_1_out, E);
  Clock clock_1 (.out(clock_1_out));
  not not_2 (not_2_out, Q_2);
  J_K_Flip_Flop j_k_ff_1 (.J(E), .clk(clock_1_out), .K(E), .Q(Q_2), .Qn(Q_prime_2));  // open: preset, en, reset
  J_K_Flip_Flop j_k_ff_2 (
    .J(and_3_out), .clk(clock_1_out), .K(and_3_out), .Q(Q), .Qn(Q_prime));  // open: preset, en, reset

  // Notes on the sheet:
  //   Clock
  //   B
  //   A
endmodule
