// Logisim project main.circ as structural Verilog: 16 circuits, main circuit main
module main (
  input  [3:0] A3_A0,
  input  [3:0] B3_B0,
  input  S0,
  input  S1,
  input  M,
  output Co,
  output V,
  output Cs,
  output out_9,
  output out_10,
  output out_11,
  output out_12,
  output out_13,
  output A___B,
  output out_15
);

  wire alu_1_f, alu_1_out_10, alu_1_out_11, alu_1_out_12, decoder_w_mode_1_a, decoder_w_mode_1_b,
       decoder_w_mode_1_c, decoder_w_mode_1_d, decoder_w_mode_1_e, decoder_w_mode_1_f, decoder_w_mode_1_g;

  ALU alu_1 (
    .A3_A0(A3_A0), .B3_B0(B3_B0), .S0(S0), .S1(S1), .Co(Co), .Overflow(V), .Cs(Cs), .F(alu_1_f),
    .out_10(alu_1_out_10), .out_11(alu_1_out_11), .out_12(alu_1_out_12), .A___B(out_15), .A___B_2(A___B),
    .A___B_3(out_13), .M(M));
  Decoder_w__Mode decoder_w_mode_1 (
    .F0(alu_1_f), .F1(alu_1_out_10), .F2(alu_1_out_11), .F3(alu_1_out_12), .M(M), .a(decoder_w_mode_1_a),
    .b(decoder_w_mode_1_b), .c(decoder_w_mode_1_c), .d(decoder_w_mode_1_d), .e(decoder_w_mode_1_e),
    .f(decoder_w_mode_1_f), .g(decoder_w_mode_1_g), .LED1(out_9), .LED2(out_10), .LED3(out_11), .LED4(out_12));
  _7_Segment_Display u_7_segment_display_1 (
    .g(decoder_w_mode_1_g), .f(decoder_w_mode_1_f), .a(decoder_w_mode_1_a), .b(decoder_w_mode_1_b),
    .e(decoder_w_mode_1_e), .d(decoder_w_mode_1_d), .c(decoder_w_mode_1_c), .dp(1'b0));

  // Notes on the sheet:
  //   Data
  //   Selection
  //   Mode
  //   Carry
  //   Overflow
  //   F (Result)
  //   Comparator
  //   A < B
  //   A > b
  //   LED Result
endmodule

// 4-7 Decoder w/Mode
module Decoder_w__Mode (
  input  F0,
  input  F1,
  input  F2,
  input  F3,
  input  M,
  output a,
  output b,
  output c,
  output d,
  output e,
  output f,
  output g,
  output LED1,
  output LED2,
  output LED3,
  output LED4
);

  wire and_5_out, and_6_out, and_7_out, and_8_out, not_1_out;

  not not_1 (not_1_out, M);
  and and_1 (LED1, F0, M);
  and and_2 (LED2, F1, M);
  and and_3 (LED3, F2, M);
  and and_4 (LED4, F3, M);
  and and_5 (and_5_out, F0, not_1_out);
  and and_6 (and_6_out, F1, not_1_out);
  and and_7 (and_7_out, F2, not_1_out);
  and and_8 (and_8_out, F3, not_1_out);
  _4_7_Decoder u_4_7_decoder_1 (
    .F0(and_5_out), .F1(and_6_out), .F2(and_7_out), .F3(and_8_out), .a(a), .b(b), .c(c), .d(d), .e(e), .f(f),
    .g(g));
endmodule

module _4_7_Decoder (
  input  F0,
  input  F1,
  input  F2,
  input  F3,
  output a,
  output b,
  output c,
  output d,
  output e,
  output f,
  output g
);

  wire and_1_out, and_2_out, and_3_out, and_4_out, and_5_out, and_6_out, and_7_out, and_8_out, and_9_out,
       and_10_out, and_11_out, and_12_out, and_13_out, and_14_out, and_15_out, and_16_out, and_17_out,
       and_18_out, and_19_out, and_20_out, and_21_out, and_22_out, and_23_out, and_24_out, and_25_out,
       and_26_out, and_27_out, and_28_out, and_29_out, and_30_out, and_31_out, and_32_out, and_33_out,
       and_34_out, and_35_out, not_1_out, not_2_out, not_3_out, not_4_out, not_5_out, not_6_out, not_7_out,
       not_8_out, not_9_out, not_10_out, not_11_out, not_12_out, not_13_out, not_14_out, not_15_out,
       not_16_out, not_17_out, not_18_out, not_19_out, not_20_out, not_21_out, not_22_out, not_23_out,
       not_24_out, not_25_out, not_26_out, not_27_out, not_28_out, not_29_out, not_30_out, not_31_out,
       not_32_out, not_33_out, not_34_out, not_35_out, not_36_out, not_37_out, not_38_out, not_39_out,
       not_40_out, not_41_out, not_42_out, not_43_out, not_44_out;

  not not_1 (not_1_out, F1);
  and and_1 (and_1_out, not_1_out, not_2_out);
  not not_2 (not_2_out, F3);
  not not_3 (not_3_out, F0);
  and and_2 (and_2_out, not_3_out, F2);
  not not_4 (not_4_out, F0);
  and and_3 (and_3_out, not_4_out, F1, F3);
  and and_4 (and_4_out, F1, F2);
  and and_5 (and_5_out, F0, not_5_out, not_6_out);
  not not_5 (not_5_out, F1);
  not not_6 (not_6_out, F2);
  and and_6 (and_6_out, F0, not_7_out);
  not not_7 (not_7_out, F3);
  not not_8 (not_8_out, F0);
  and and_7 (and_7_out, not_8_out, not_9_out);
  not not_9 (not_9_out, F1);
  not not_10 (not_10_out, F0);
  not not_11 (not_11_out, F2);
  and and_8 (and_8_out, not_10_out, not_11_out, not_12_out);
  not not_12 (not_12_out, F3);
  not not_13 (not_13_out, F1);
  and and_9 (and_9_out, not_13_out, not_14_out);
  not not_14 (not_14_out, F3);
  not not_15 (not_15_out, F0);
  and and_10 (and_10_out, not_15_out, F2, F3);
  not not_16 (not_16_out, F2);
  and and_11 (and_11_out, F0, not_16_out, F3);
  not not_17 (not_17_out, F0);
  and and_12 (and_12_out, not_17_out, not_18_out);
  not not_18 (not_18_out, F2);
  not not_19 (not_19_out, F0);
  and and_13 (and_13_out, not_19_out, F3);
  not not_20 (not_20_out, F2);
  and and_14 (and_14_out, not_20_out, F3);
  not not_21 (not_21_out, F0);
  and and_15 (and_15_out, not_21_out, F1);
  and and_16 (and_16_out, F0, not_22_out);
  not not_22 (not_22_out, F1);
  not not_23 (not_23_out, F0);
  not not_24 (not_24_out, F1);
  and and_17 (and_17_out, not_23_out, not_24_out, not_25_out);
  not not_25 (not_25_out, F3);
  not not_26 (not_26_out, F1);
  and and_18 (and_18_out, not_26_out, F2, F3);
  and and_19 (and_19_out, F1, not_27_out, F3);
  not not_27 (not_27_out, F2);
  and and_20 (and_20_out, F1, F2, not_28_out);
  not not_28 (not_28_out, F3);
  not not_29 (not_29_out, F2);
  and and_21 (and_21_out, F0, not_29_out, not_30_out);
  not not_30 (not_30_out, F3);
  not not_31 (not_31_out, F1);
  and and_22 (and_22_out, not_31_out, not_32_out);
  not not_32 (not_32_out, F3);
  and and_23 (and_23_out, F2, not_33_out);
  not not_33 (not_33_out, F3);
  and and_24 (and_24_out, F0, F2);
  and and_25 (and_25_out, F0, F1);
  not not_34 (not_34_out, F2);
  and and_26 (and_26_out, not_34_out, not_35_out);
  not not_35 (not_35_out, F3);
  not not_36 (not_36_out, F0);
  and and_27 (and_27_out, not_36_out, F1, not_37_out);
  not not_37 (not_37_out, F2);
  and and_28 (and_28_out, F1, not_38_out);
  not not_38 (not_38_out, F3);
  and and_29 (and_29_out, F0, not_39_out);
  not not_39 (not_39_out, F1);
  and and_30 (and_30_out, F0, F2);
  not not_40 (not_40_out, F1);
  and and_31 (and_31_out, not_40_out, F2);
  and and_32 (and_32_out, F2, not_41_out);
  not not_41 (not_41_out, F3);
  not not_42 (not_42_out, F0);
  and and_33 (and_33_out, not_42_out, F1, not_43_out);
  not not_43 (not_43_out, F2);
  and and_34 (and_34_out, F0, not_44_out);
  not not_44 (not_44_out, F1);
  and and_35 (and_35_out, F0, F3);
  or or_1 (b, and_7_out, and_8_out, and_9_out, and_10_out, and_11_out);
  or or_2 (c, and_12_out, and_13_out, and_14_out, and_15_out, and_16_out);
  or or_3 (d, and_17_out, and_18_out, and_19_out, and_20_out, and_21_out);
  or or_4 (e, and_22_out, and_23_out, and_24_out, and_25_out);
  or or_5 (f, and_26_out, and_27_out, and_28_out, and_29_out, and_30_out);
  or or_6 (g, and_31_out, and_32_out, and_33_out, and_34_out, and_35_out);
  or or_7 (a, and_1_out, and_2_out, and_3_out, and_4_out, and_5_out, and_6_out);
endmodule

// 4-Bit ALU
module ALU (
  input  [3:0] A3_A0,
  input  [3:0] B3_B0,
  input  S0,
  input  S1,
  input  M,
  output Co,
  output Overflow,
  output Cs,
  output F,
  output out_10,
  output out_11,
  output out_12,
  output A___B,
  output A___B_2,
  output A___B_3
);

  wire [3:0] arithmetic_unit_1_fa, logic_unit_1_fb;

  Arithmetic_Unit arithmetic_unit_1 (
    .A3_A0(A3_A0), .B3_B0(B3_B0), .Fa(arithmetic_unit_1_fa), .Co(Co), .S0(S0), .S1(S1), .Overflow(Overflow),
    .Cs(Cs));
  Logic_Unit logic_unit_1 (.A4_A7(A3_A0), .B4_B7(B3_B0), .S0(S0), .S1(S1), .Fb(logic_unit_1_fb));
  Comp comp_1 (
    .A0(A3_A0[0]), .B0(B3_B0[0]), .A1(A3_A0[1]), .B1(B3_B0[2]), .A2(A3_A0[2]), .B2(B3_B0[1]), .A3(A3_A0[3]),
    .B3(B3_B0[3]), .A___B(A___B_2), .A___B_2(A___B), .A___B_3(A___B_3));
  _2x4_MUX u_2x4_mux_1 (
    .F0(arithmetic_unit_1_fa[3]), .F1(arithmetic_unit_1_fa[2]), .F2(arithmetic_unit_1_fa[1]),
    .F3(arithmetic_unit_1_fa[0]), .F4(logic_unit_1_fb[3]), .F5(logic_unit_1_fb[2]), .F6(logic_unit_1_fb[1]),
    .F7(logic_unit_1_fb[0]), .M(M), .Y0(F), .Y1(out_10), .Y2(out_11), .Y3(out_12));

  // Notes on the sheet:
  //   Fa
  //   Fb
endmodule

module Arithmetic_Unit (
  input  [3:0] A3_A0,
  input  [3:0] B3_B0,
  input  S0,
  input  S1,
  output Co,
  output Overflow,
  output Cs,
  output [3:0] Fa
);

  wire adder_unit_1_s0, adder_unit_1_s1, adder_unit_1_s2, adder_unit_1_s3, adder_unit_1_v, incrementor_1_s0,
       incrementor_1_s1, incrementor_1_s2, incrementor_1_s3, incrementor_1_v, n2_s_comp_negator_1_s0,
       n2_s_comp_negator_1_s1, n2_s_comp_negator_1_s2, n2_s_comp_negator_1_s3, n2_s_comp_negator_1_v,
       subtractor_unit_1_s0, subtractor_unit_1_s1, subtractor_unit_1_s2, subtractor_unit_1_s3,
       subtractor_unit_1_v;

  Adder_Unit adder_unit_1 (
    .Cout(Co), .V(adder_unit_1_v), .B3(B3_B0[3]), .A3(A3_A0[3]), .B2(B3_B0[2]), .A2(A3_A0[2]), .B1(B3_B0[1]),
    .A1(A3_A0[1]), .B0(B3_B0[0]), .A0(A3_A0[0]), .S3(adder_unit_1_s3), .S2(adder_unit_1_s2),
    .S1(adder_unit_1_s1), .S0(adder_unit_1_s0));
  _2_s_Comp_Negator u_2_s_comp_negator_1 (
    .B3(B3_B0[3]), .B2(B3_B0[2]), .B1(B3_B0[1]), .B0(B3_B0[0]), .S3(n2_s_comp_negator_1_s3),
    .S2(n2_s_comp_negator_1_s2), .S1(n2_s_comp_negator_1_s1), .S0(n2_s_comp_negator_1_s0),
    .V(n2_s_comp_negator_1_v));
  Incrementor incrementor_1 (
    .A3(A3_A0[3]), .A2(A3_A0[2]), .A1(A3_A0[1]), .A0(A3_A0[0]), .S3(incrementor_1_s3), .S2(incrementor_1_s2),
    .S1(incrementor_1_s1), .S0(incrementor_1_s0), .V(incrementor_1_v));
  Subtractor_Unit subtractor_unit_1 (
    .Cout(Cs), .V(subtractor_unit_1_v), .B3(B3_B0[3]), .A3(A3_A0[3]), .B2(B3_B0[2]), .A2(A3_A0[2]),
    .B1(B3_B0[1]), .A1(A3_A0[1]), .B0(B3_B0[0]), .A0(A3_A0[0]), .S3(subtractor_unit_1_s3),
    .S2(subtractor_unit_1_s2), .S1(subtractor_unit_1_s1), .S0(subtractor_unit_1_s0));
  or or_1 (Overflow, adder_unit_1_v, n2_s_comp_negator_1_v, incrementor_1_v, subtractor_unit_1_v);
  _16x4_MUX u_16x4_mux_1 (
    .A4(adder_unit_1_s0), .A5(adder_unit_1_s1), .A6(adder_unit_1_s2), .A7(adder_unit_1_s3),
    .B4(subtractor_unit_1_s0), .B5(subtractor_unit_1_s1), .B6(subtractor_unit_1_s2),
    .B7(subtractor_unit_1_s3), .C4(n2_s_comp_negator_1_s0), .C5(n2_s_comp_negator_1_s1),
    .C6(n2_s_comp_negator_1_s2), .C7(n2_s_comp_negator_1_s3), .D4(incrementor_1_s0), .D5(incrementor_1_s1),
    .D6(incrementor_1_s2), .D7(incrementor_1_s3), .S0(S0), .S1(S1), .Y4(Fa[0]), .Y5(Fa[1]), .Y6(Fa[2]),
    .Y7(Fa[3]));
endmodule

module Logic_Unit (
  input  [3:0] A4_A7,
  input  [3:0] B4_B7,
  input  S0,
  input  S1,
  output [3:0] Fb
);

  wire [3:0] and_1_out, not_1_out, or_1_out, xor_1_out;

  assign and_1_out = A4_A7 & B4_B7;  // AND_Gate and_1, 4 bits wide
  assign or_1_out = A4_A7 | B4_B7;  // OR_Gate or_1, 4 bits wide
  assign xor_1_out = A4_A7 ^ B4_B7;  // XOR_Gate xor_1, 4 bits wide
  assign not_1_out = ~A4_A7;  // NOT_Gate not_1, 4 bits wide
  _16x4_MUX u_16x4_mux_1 (
    .A4(and_1_out[0]), .A5(and_1_out[1]), .A6(and_1_out[2]), .A7(and_1_out[3]), .B4(or_1_out[0]),
    .B5(or_1_out[1]), .B6(or_1_out[2]), .B7(or_1_out[3]), .C4(xor_1_out[0]), .C5(xor_1_out[1]),
    .C6(xor_1_out[2]), .C7(xor_1_out[3]), .D4(not_1_out[0]), .D5(not_1_out[1]), .D6(not_1_out[2]),
    .D7(not_1_out[3]), .S0(S0), .S1(S1), .Y4(Fb[0]), .Y5(Fb[1]), .Y6(Fb[2]), .Y7(Fb[3]));

  // Notes on the sheet:
  //   AND
  //   OR
  //   XOR
  //   1's Comp
  //   F4
  //   F5
  //   F6
  //   F7
  //   16-Channel 4-Bit MUX
endmodule

// Comparator
module Comp (
  input  A0,
  input  B0,
  input  A1,
  input  B1,
  input  A2,
  input  B2,
  input  A3,
  input  B3,
  output A___B,
  output A___B_2,
  output A___B_3
);

  wire and_1_out, and_2_out, and_3_out, and_4_out, and_5_out, and_6_out, and_7_out, and_8_out, and_10_out,
       and_11_out, and_12_out, and_13_out, and_14_out, and_15_out, nor_1_out, nor_2_out, nor_3_out,
       nor_4_out, not_1_out, not_2_out, not_3_out, not_4_out, not_5_out, not_6_out, not_7_out, not_8_out;

  not not_1 (not_1_out, A0);
  not not_2 (not_2_out, B0);
  not not_3 (not_3_out, A1);
  not not_4 (not_4_out, B1);
  not not_5 (not_5_out, A2);
  not not_6 (not_6_out, B2);
  not not_7 (not_7_out, A3);
  not not_8 (not_8_out, B3);
  and and_1 (and_1_out, not_1_out, B0);
  and and_2 (and_2_out, A0, not_2_out);
  and and_3 (and_3_out, not_3_out, B1);
  and and_4 (and_4_out, A1, not_4_out);
  and and_5 (and_5_out, not_5_out, B2);
  and and_6 (and_6_out, A2, not_6_out);
  and and_7 (and_7_out, not_7_out, B3);
  and and_8 (and_8_out, A3, not_8_out);
  nor nor_1 (nor_1_out, and_1_out, and_2_out);
  nor nor_2 (nor_2_out, and_3_out, and_4_out);
  nor nor_3 (nor_3_out, and_5_out, and_6_out);
  nor nor_4 (nor_4_out, and_7_out, and_8_out);
  and and_9 (A___B, nor_1_out, nor_2_out, nor_3_out, nor_4_out);
  and and_10 (and_10_out, and_2_out, nor_2_out, nor_3_out, nor_4_out);
  and and_11 (and_11_out, and_4_out, nor_3_out, nor_4_out);
  and and_12 (and_12_out, and_6_out, nor_4_out);
  or or_1 (A___B_2, and_10_out, and_11_out, and_12_out, and_8_out);
  and and_13 (and_13_out, nor_4_out, and_5_out);
  and and_14 (and_14_out, and_3_out, nor_4_out, nor_3_out);
  and and_15 (and_15_out, and_1_out, nor_2_out, nor_3_out, nor_4_out, nor_4_out);
  or or_2 (A___B_3, and_15_out, and_14_out, and_13_out, and_7_out);
endmodule

module _16x4_MUX (
  input  A4,
  input  A5,
  input  A6,
  input  A7,
  input  B4,
  input  B5,
  input  B6,
  input  B7,
  input  C4,
  input  C5,
  input  C6,
  input  C7,
  input  D4,
  input  D5,
  input  D6,
  input  D7,
  input  S0,
  input  S1,
  output Y4,
  output Y5,
  output Y6,
  output Y7
);

  wire and_1_out, and_2_out, and_3_out, and_4_out, and_5_out, and_6_out, and_7_out, and_8_out, and_9_out,
       and_10_out, and_11_out, and_12_out, and_13_out, and_14_out, and_15_out, and_16_out, not_1_out,
       not_2_out, not_3_out;

  not not_1 (not_1_out, S0);
  not not_2 (not_2_out, not_1_out);
  not not_3 (not_3_out, S1);
  and and_1 (and_1_out, A4, not_1_out, not_3_out);
  and and_2 (and_2_out, A5, not_1_out, not_3_out);
  and and_3 (and_3_out, A6, not_1_out, not_3_out);
  and and_4 (and_4_out, A7, not_1_out, not_3_out);
  and and_5 (and_5_out, B4, not_1_out, S1);
  and and_6 (and_6_out, B5, not_1_out, S1);
  and and_7 (and_7_out, B6, not_1_out, S1);
  and and_8 (and_8_out, B7, not_1_out, S1);
  and and_9 (and_9_out, C4, not_2_out, not_3_out);
  and and_10 (and_10_out, C5, not_2_out, not_3_out);
  and and_11 (and_11_out, C6, not_2_out, not_3_out);
  and and_12 (and_12_out, C7, not_2_out, not_3_out);
  and and_13 (and_13_out, D4, not_2_out, S1);
  and and_14 (and_14_out, D5, not_2_out, S1);
  and and_15 (and_15_out, D6, not_2_out, S1);
  and and_16 (and_16_out, D7, not_2_out, S1);
  or or_1 (Y4, and_1_out, and_5_out, and_9_out, and_13_out);
  or or_2 (Y5, and_2_out, and_6_out, and_10_out, and_14_out);
  or or_3 (Y6, and_3_out, and_7_out, and_11_out, and_15_out);
  or or_4 (Y7, and_4_out, and_8_out, and_12_out, and_16_out);
endmodule

// 2 Channel 4 Bit MUX
module _2x4_MUX (
  input  F0,
  input  F1,
  input  F2,
  input  F3,
  input  F4,
  input  F5,
  input  F6,
  input  F7,
  input  M,
  output Y0,
  output Y1,
  output Y2,
  output Y3
);

  wire and_1_out, and_2_out, and_3_out, and_4_out, and_5_out, and_6_out, and_7_out, and_8_out, not_1_out,
       not_2_out;

  not not_1 (not_1_out, M);
  not not_2 (not_2_out, not_1_out);
  and and_1 (and_1_out, F0, not_1_out);
  and and_2 (and_2_out, F1, not_1_out);
  and and_3 (and_3_out, F2, not_1_out);
  and and_4 (and_4_out, F3, not_1_out);
  and and_5 (and_5_out, F4, not_2_out);
  and and_6 (and_6_out, F5, not_2_out);
  and and_7 (and_7_out, F6, not_2_out);
  and and_8 (and_8_out, F7, not_2_out);
  or or_1 (Y0, and_1_out, and_5_out);
  or or_2 (Y1, and_2_out, and_6_out);
  or or_3 (Y2, and_3_out, and_7_out);
  or or_4 (Y3, and_4_out, and_8_out);
endmodule

// Adder
module Adder_Unit (
  input  B3,
  input  A3,
  input  B2,
  input  A2,
  input  B1,
  input  A1,
  input  B0,
  input  A0,
  output Cout,
  output V,
  output S3,
  output S2,
  output S1,
  output S0
);

  wire full_adder_2_cout, full_adder_3_cout, full_adder_4_cout;

  xor xor_1 (V, Cout, full_adder_2_cout);
  Full_Adder full_adder_1 (.A(A3), .B(B3), .Cin(full_adder_2_cout), .S(S3), .Cout(Cout));
  Full_Adder full_adder_2 (.A(A2), .B(B2), .Cin(full_adder_3_cout), .S(S2), .Cout(full_adder_2_cout));
  Full_Adder full_adder_3 (.A(A1), .B(B1), .Cin(full_adder_4_cout), .S(S1), .Cout(full_adder_3_cout));
  Full_Adder full_adder_4 (.A(A0), .B(B0), .Cin(1'b0), .S(S0), .Cout(full_adder_4_cout));
endmodule

module Full_Adder (
  input  A,
  input  B,
  input  Cin,
  output S,
  output Cout
);

  wire and_1_out, and_2_out, xor_1_out;

  xor xor_1 (xor_1_out, A, B);
  and and_1 (and_1_out, A, B);
  xor xor_2 (S, xor_1_out, Cin);
  and and_2 (and_2_out, xor_1_out, Cin);
  or or_1 (Cout, and_2_out, and_1_out);
endmodule

// Subtractor
module Subtractor_Unit (
  input  B3,
  input  A3,
  input  B2,
  input  A2,
  input  B1,
  input  A1,
  input  B0,
  input  A0,
  output Cout,
  output V,
  output S3,
  output S2,
  output S1,
  output S0
);

  wire full_adder_2_cout, full_adder_3_cout, full_adder_4_cout, not_1_out, not_2_out, not_3_out, not_4_out;

  xor xor_1 (V, Cout, full_adder_2_cout);
  not not_1 (not_1_out, B3);
  Full_Adder full_adder_1 (.A(A3), .B(not_1_out), .Cin(full_adder_2_cout), .S(S3), .Cout(Cout));
  not not_2 (not_2_out, B2);
  Full_Adder full_adder_2 (.A(A2), .B(not_2_out), .Cin(full_adder_3_cout), .S(S2), .Cout(full_adder_2_cout));
  not not_3 (not_3_out, B1);
  Full_Adder full_adder_3 (.A(A1), .B(not_3_out), .Cin(full_adder_4_cout), .S(S1), .Cout(full_adder_3_cout));
  not not_4 (not_4_out, B0);
  Full_Adder full_adder_4 (.A(A0), .B(not_4_out), .Cin(1'b1), .S(S0), .Cout(full_adder_4_cout));

  // Notes on the sheet:
  //   Cin
endmodule

// 2' Complement Negator
module _2_s_Comp_Negator (
  input  B3,
  input  B2,
  input  B1,
  input  B0,
  output V,
  output S3,
  output S2,
  output S1,
  output S0
);

  wire full_adder_1_cout, full_adder_2_cout, full_adder_3_cout, full_adder_4_cout, not_1_out, not_2_out,
       not_3_out, not_4_out;

  xor xor_1 (V, full_adder_1_cout, full_adder_2_cout);
  not not_1 (not_1_out, B3);
  Full_Adder full_adder_1 (.A(1'b0), .B(not_1_out), .Cin(full_adder_2_cout), .S(S3), .Cout(full_adder_1_cout));
  not not_2 (not_2_out, B2);
  Full_Adder full_adder_2 (.A(1'b0), .B(not_2_out), .Cin(full_adder_3_cout), .S(S2), .Cout(full_adder_2_cout));
  not not_3 (not_3_out, B1);
  Full_Adder full_adder_3 (.A(1'b0), .B(not_3_out), .Cin(full_adder_4_cout), .S(S1), .Cout(full_adder_3_cout));
  not not_4 (not_4_out, B0);
  Full_Adder full_adder_4 (.A(1'b0), .B(not_4_out), .Cin(1'b1), .S(S0), .Cout(full_adder_4_cout));
endmodule

module Incrementor (
  input  A3,
  input  A2,
  input  A1,
  input  A0,
  output V,
  output S3,
  output S2,
  output S1,
  output S0
);

  wire full_adder_1_cout, full_adder_2_cout, full_adder_3_cout, full_adder_4_cout;

  xor xor_1 (V, full_adder_1_cout, full_adder_2_cout);
  Full_Adder full_adder_1 (.A(1'b0), .B(A3), .Cin(full_adder_2_cout), .S(S3), .Cout(full_adder_1_cout));
  Full_Adder full_adder_2 (.A(1'b0), .B(A2), .Cin(full_adder_3_cout), .S(S2), .Cout(full_adder_2_cout));
  Full_Adder full_adder_3 (.A(1'b0), .B(A1), .Cin(full_adder_4_cout), .S(S1), .Cout(full_adder_3_cout));
  Full_Adder full_adder_4 (.A(1'b0), .B(A0), .Cin(1'b1), .S(S0), .Cout(full_adder_4_cout));
endmodule

// Adder
module Adder___Subtractor_Unit (
  input  B3,
  input  A3,
  input  B2,
  input  A2,
  input  B1,
  input  A1,
  input  B0,
  input  A0,
  input  Cin,
  output Cout,
  output Overflow,
  output S3,
  output S2,
  output S1,
  output S0
);

  wire full_adder_2_cout, full_adder_3_cout, full_adder_4_cout, xor_2_out, xor_3_out, xor_4_out, xor_5_out;

  xor xor_1 (Overflow, Cout, full_adder_2_cout);
  xor xor_2 (xor_2_out, B3, Cin);
  Full_Adder full_adder_1 (.A(A3), .B(xor_2_out), .Cin(full_adder_2_cout), .S(S3), .Cout(Cout));
  xor xor_3 (xor_3_out, B2, Cin);
  Full_Adder full_adder_2 (.A(A2), .B(xor_3_out), .Cin(full_adder_3_cout), .S(S2), .Cout(full_adder_2_cout));
  xor xor_4 (xor_4_out, B1, Cin);
  Full_Adder full_adder_3 (.A(A1), .B(xor_4_out), .Cin(full_adder_4_cout), .S(S1), .Cout(full_adder_3_cout));
  xor xor_5 (xor_5_out, B0, Cin);
  Full_Adder full_adder_4 (.A(A0), .B(xor_5_out), .Cin(Cin), .S(S0), .Cout(full_adder_4_cout));
endmodule

module Comparator (
  input  A0,
  input  B0,
  input  A1,
  input  B1,
  input  A2,
  input  B2,
  input  A3,
  input  B3,
  output A___B,
  output A___B_2
);

  wire and_4_out, and_5_out, and_6_out, and_7_out, not_3_out, not_4_out, not_5_out, not_6_out, not_7_out,
       not_8_out, xor_1_out, xor_2_out, xor_3_out, xor_4_out;

  // NOT_Gate not_1 is placed but not wired
  // NOT_Gate not_2 is placed but not wired
  // AND_Gate and_1 is placed but not wired
  // AND_Gate and_2 is placed but not wired
  xor xor_1 (xor_1_out, A0, B0);
  not not_3 (not_3_out, xor_1_out);
  not not_4 (not_4_out, xor_2_out);
  xor xor_2 (xor_2_out, A1, B1);
  xor xor_3 (xor_3_out, A2, B2);
  not not_5 (not_5_out, xor_3_out);
  not not_6 (not_6_out, xor_4_out);
  xor xor_4 (xor_4_out, A3, B3);
  // NOR_Gate nor_1 is placed but not wired
  and and_3 (A___B_2, not_3_out, not_4_out, not_5_out, not_6_out);
  // AND_Gate and_4 has open pins: out=and_4_out
  // AND_Gate and_5 has open pins: out=and_5_out
  and and_6 (and_6_out, not_7_out, A2);
  not not_7 (not_7_out, B2);
  not not_8 (not_8_out, B3);
  and and_7 (and_7_out, not_8_out, A3);
  or or_1 (A___B, and_4_out, and_5_out, and_6_out, and_7_out);
endmodule
