// Logisim project lab4q2d.circ as structural Verilog: 1 circuit, main circuit main
module main (
  input  X,
  input  Y,
  input  Z,
  input  W,
  output out_5
);

  wire nand_1_out, nand_2_out, nand_3_out, nand_4_out, nand_5_out, not_1_out, not_2_out, not_3_out;

  not not_1 (not_1_out, X);
  not not_2 (not_2_out, Y);
  not not_3 (not_3_out, Z);
  nand nand_1 (nand_1_out, not_1_out, not_3_out);
  nand nand_2 (nand_2_out, not_1_out, W);
  nand nand_3 (nand_3_out, not_1_out, Y);
  nand nand_4 (nand_4_out, not_3_out, W);
  nand nand_5 (nand_5_out, X, not_2_out);
  nand nand_6 (out_5, nand_1_out, nand_2_out, nand_3_out, nand_4_out, nand_5_out);
endmodule
