// Logisim project lab4q2d2.circ as structural Verilog: 1 circuit, main circuit main
module main (
  input  [3:0] in_1
);

  Hex_Digit_Display hex_digit_display_1 (.value(in_1), .dp(1'b0));
endmodule
